# Fritzing sketch LedStrip12V (saved by Fritzing 0.9.2b)

parts:
  R2 = Resistor [tolerance=±5% resistance=470 package=THT]
  R1 = Resistor [tolerance=±5% resistance=470 package=THT]
  R3 = Resistor [tolerance=±5% resistance=470 package=THT]
  JACK1 = 2.1mm Barrel Jack with Terminal Block
  U1 = ESP8266 WiFi Module [part_number=ESP8266]
  Analog_RGB_LED_Strip1 = Analog RGB LED Strip
  Q1 = TIP120 Hi-Current Darlington Transistor
  Q2 = TIP120 Hi-Current Darlington Transistor
  Q3 = TIP120 Hi-Current Darlington Transistor
  REG1 = LD33 Low-Dropout Voltage Regulator
  C1 = Electrolytic Capacitor [capacitance=1µF package="100 mil [THT, electrolytic]"]
  C2 = Electrolytic Capacitor [capacitance=1µF package="100 mil [THT, electrolytic]"]  # not connected
  S3 = Pushbutton [package="[THT]"]

nets:
  N1: R2.Pin_1, U1.GPIO_12
  N2: R1.Pin_0, U1.GPIO_14
  N3: R3.Pin_1, U1.GPIO_13
  12V: JACK1.POS, Analog_RGB_LED_Strip1.12v, REG1.Vin
  N4: U1.VCC, U1.CH_PD, REG1.Vout, C1.+
  N5: U1.GPIO_0, S3.Pin_4
  GND: U1.GND, U1.GPIO_15, Q1.EMITTER, REG1.GND, C1.-, S3.Pin_2
  N6: Analog_RGB_LED_Strip1.G, Q1.COLLECTOR
  N7: Analog_RGB_LED_Strip1.R, Q2.COLLECTOR
  N8: Analog_RGB_LED_Strip1.B, Q3.COLLECTOR

notes:
  TO LED STRIP
  To 12V Power

custom parts:
  ESP8266 WiFi Module: Generic WiFi Module based on the ESP8266 with onboard PCB antenna and UART communications
  Analog RGB LED Strip: Analog RGB LED strip
